# Fritzing sketch schaltung (saved by Fritzing 0.9.3b)
breadboards: 1

parts:
  U1 = 74HC595 [package="DIP16 [THT]"]
  Raspberry_Pi_B_rev1 = Raspberry Pi B rev1

nets:
  GND: U1.GND, Raspberry_Pi_B_rev1.GND
  N1: U1.SH_CP, Raspberry_Pi_B_rev1.GPIO_17
  N2: U1.ST_CP, Raspberry_Pi_B_rev1.GPIO_18
  N3: U1.OE, Raspberry_Pi_B_rev1.GPIO_21
  N4: U1.DS, Raspberry_Pi_B_rev1.GPIO_4
  VCC: U1.VCC, Raspberry_Pi_B_rev1.3V3
