# Fritzing sketch schaltung_mpu6050 (saved by Fritzing 0.9.3b)
breadboards: 1

parts:
  Raspberry_Pi_B_rev1 = Raspberry Pi B rev1
  GY1 = MPU-6050 GY-521 [form="♀ (female)"]

nets:
  N1: Raspberry_Pi_B_rev1.3V3, GY1.connector0
  N2: Raspberry_Pi_B_rev1.GPIO_0, GY1.connector3
  N3: Raspberry_Pi_B_rev1.GPIO_1, GY1.connector2
  N4: Raspberry_Pi_B_rev1.GND, GY1.connector1
