# Fritzing sketch schaltung (saved by Fritzing 0.9.3b)

parts:
  Raspberry_Pi1 = Raspberry Pi B rev2
  J1 = Basic Servo

nets:
  5V: Raspberry_Pi1.5V, J1.vcc
  GND: Raspberry_Pi1.GND, J1.gnd
  N1: Raspberry_Pi1.GPIO_17, J1.pulse
